// Logisim project control_logic.circ as structural Verilog: 1 circuit, main circuit control_logic
module control_logic (
  input  [1:0] bytePos,
  input  [31:0] Reg2Data,
  input  [31:0] Reg1Data,
  input  [31:0] inst,
  input  BrEq,
  input  BrLt,
  input  [31:0] MEM_READ_DATA,
  output [31:0] SwriteData,
  output [31:0] load_read_data,
  output PCSel,
  output RegWEn,
  output [2:0] ImmSel,
  output BrUn,
  output ASel,
  output BSel,
  output [3:0] ALUSel,
  output MemRW,
  output [1:0] WBSel,
  output CSRSel,
  output CSRWen,
  output [4:0] rs1,
  output [4:0] rs2,
  output [4:0] rd,
  output [3:0] WRITE_ENABLE
);

  wire B_PCSel, eq, gt, lt, or_1_out, or_2_out, or_3_out, ueq, ugt, ult;
  wire [3:0] IaluSel, LorA, multiplexer_15_out, RaluSel, RW, sbEnable, shEnable;
  wire [7:0] multiplexer_16_out;
  wire [15:0] multiplexer_17_out;
  wire [31:0] bit_extender_1_out, load_byte, load_half_data, sbWriteData, shWriteData;

  Multiplexer #(.enable("false"), .select(5), .width(4)) multiplexer_1 (
    .in0(4'b0000), .in1(4'b1010), .in2(4'b1100), .in4(4'b0110), .in5(4'b1110), .in8(4'b0111), .in13(4'b1011),
    .in16(4'b0011), .in20(4'b0100), .in22(4'b0101), .in24(4'b0010), .in28(4'b0001), .out(RaluSel),
    .sel({inst[14:12], inst[30], inst[25]}));  // open: in3, in6, in7, in9, in10, in11, in12, in14, in15, in17, in18, in19, in21, in23, in25, in26, in27, in29, in30, in31
  Multiplexer #(.enable("false"), .width(4)) multiplexer_2 (.in0(IaluSel), .in1(RaluSel), .out(ALUSel), .sel(inst[5]));
  Multiplexer #(.enable("false"), .width(4)) multiplexer_3 (.in0(4'b0100), .in1(4'b0101), .out(LorA), .sel(inst[30]));
  Multiplexer #(.enable("false"), .select(5)) multiplexer_4 (
    .in0(1'b1), .in4(1'b1), .in5(1'b1), .in8(1'b0), .in12(1'b1), .in13(1'b1), .in24(1'b0), .in25(1'b1),
    .in27(1'b1), .in28(1'b0), .out(RegWEn), .sel(inst[6:2]));  // open: in1, in2, in3, in6, in7, in9, in10, in11, in14, in15, in16, in17, in18, in19, in20, in21, in22, in23, in26, in29, in30, in31
  Multiplexer #(.enable("false"), .select(5)) multiplexer_5 (
    .in0(1'b0), .in4(1'b0), .in5(1'b0), .in8(1'b0), .in12(1'b0), .in13(1'b0), .in24(B_PCSel), .in25(1'b1),
    .in27(1'b1), .in28(1'b0), .out(PCSel), .sel(inst[6:2]));  // open: in1, in2, in3, in6, in7, in9, in10, in11, in14, in15, in16, in17, in18, in19, in20, in21, in22, in23, in26, in29, in30, in31
  Multiplexer #(.enable("false"), .select(5), .width(3)) multiplexer_6 (
    .in0(3'b000), .in4(3'b000), .in5(3'b011), .in8(3'b001), .in13(3'b100), .in24(3'b010), .in25(3'b000),
    .in27(3'b101), .in28(3'b000), .out(ImmSel), .sel(inst[6:2]));  // open: in1, in2, in3, in6, in7, in9, in10, in11, in12, in14, in15, in16, in17, in18, in19, in20, in21, in22, in23, in26, in29, in30, in31
  Multiplexer #(.enable("false"), .select(3), .width(4)) multiplexer_7 (
    .in0(4'b0000), .in1(4'b0110), .in2(4'b0111), .in4(4'b0011), .in5(LorA), .in6(4'b0010), .in7(4'b0001),
    .out(IaluSel), .sel(inst[14:12]));  // open: in3
  Comparator #(.width(32)) comparator_1 (.a(Reg1Data), .b(Reg2Data), .gt(gt), .eq(eq), .lt(lt));
  Comparator #(.mode("unsigned"), .width(32)) comparator_2 (.a(Reg1Data), .b(Reg2Data), .gt(ugt), .eq(ueq), .lt(ult));
  Comparator #(.width(7)) comparator_3 (.a(inst[6:0]), .b(7'b0100011), .eq(MemRW));  // open: gt, lt
  Multiplexer #(.enable("false"), .select(2), .width(2)) multiplexer_8 (
    .in0(2'b01), .in1(2'b00), .in2(2'b10), .in3(2'b00), .out(WBSel), .sel(inst[5:4]));
  or or_1 (or_1_out, gt, lt);
  or or_2 (or_2_out, gt, eq);
  or or_3 (or_3_out, ugt, ueq);
  Comparator #(.width(7)) comparator_4 (.a(inst[6:0]), .b(7'b1110011), .eq(CSRWen));  // open: gt, lt
  assign bit_extender_1_out = {{16{Reg2Data[15]}}, Reg2Data[15:0]};  // Bit_Extender bit_extender_1
  Multiplexer #(.enable("false"), .select(3)) multiplexer_9 (
    .in0(eq), .in1(or_1_out), .in4(lt), .in5(or_2_out), .in6(ult), .in7(or_3_out), .out(B_PCSel),
    .sel(inst[14:12]));  // open: in2, in3
  Multiplexer #(.enable("false"), .select(2), .width(32)) multiplexer_10 (
    .in0(bit_extender_1_out), .in1({{8{1'b0}}, Reg2Data[15:0], {8{1'b0}}}),
    .in2({Reg2Data[15:0], {16{1'b0}}}), .out(shWriteData), .sel(bytePos));  // open: in3
  Multiplexer #(.enable("false"), .width(8)) multiplexer_11 (
    .in0({8{1'b0}}), .in1(Reg2Data[7:0]), .out(sbWriteData[7:0]), .sel(WRITE_ENABLE[0]));
  Multiplexer #(.enable("false"), .width(8)) multiplexer_12 (
    .in0({8{1'b0}}), .in1(Reg2Data[7:0]), .out(sbWriteData[15:8]), .sel(WRITE_ENABLE[1]));
  Multiplexer #(.enable("false"), .width(8)) multiplexer_13 (
    .in0({8{1'b0}}), .in1(Reg2Data[7:0]), .out(sbWriteData[23:16]), .sel(WRITE_ENABLE[2]));
  Multiplexer #(.enable("false"), .width(8)) multiplexer_14 (
    .in0({8{1'b0}}), .in1(Reg2Data[7:0]), .out(sbWriteData[31:24]), .sel(WRITE_ENABLE[3]));
  Multiplexer #(.enable("false"), .select(2), .width(4)) multiplexer_15 (
    .in0(sbEnable), .in1(shEnable), .in2(4'b1111), .out(multiplexer_15_out), .sel(inst[13:12]));  // open: in3
  assign RW = {{3{MemRW}}, MemRW};  // Bit_Extender bit_extender_2
  Multiplexer #(.enable("false"), .select(2), .width(8)) multiplexer_16 (
    .in0(MEM_READ_DATA[7:0]), .in1(MEM_READ_DATA[15:8]), .in2(MEM_READ_DATA[23:16]),
    .in3(MEM_READ_DATA[31:24]), .out(multiplexer_16_out), .sel(bytePos));
  assign WRITE_ENABLE = multiplexer_15_out & RW;  // AND_Gate and_1, 4 bits wide
  Multiplexer #(.enable("false"), .select(2), .width(16)) multiplexer_17 (
    .in0(MEM_READ_DATA[15:0]), .in1(MEM_READ_DATA[23:8]), .in2(MEM_READ_DATA[31:16]),
    .out(multiplexer_17_out), .sel(bytePos));  // open: in3
  assign load_half_data = {{16{multiplexer_17_out[15]}}, multiplexer_17_out};  // Bit_Extender bit_extender_3
  assign load_byte = {{24{multiplexer_16_out[7]}}, multiplexer_16_out};  // Bit_Extender bit_extender_4
  Multiplexer #(.enable("false"), .select(2), .width(32)) multiplexer_18 (
    .in0(sbWriteData), .in1(shWriteData), .in2(Reg2Data), .out(SwriteData), .sel(inst[13:12]));  // open: in3
  Multiplexer #(.enable("false"), .select(2), .width(32)) multiplexer_19 (
    .in0(load_byte), .in1(load_half_data), .in2(MEM_READ_DATA), .out(load_read_data), .sel(inst[13:12]));  // open: in3
  Multiplexer #(.enable("false"), .select(2), .width(4)) multiplexer_20 (
    .in0(4'b0001), .in1(4'b0010), .in2(4'b0100), .in3(4'b1000), .out(sbEnable), .sel(bytePos));
  Multiplexer #(.enable("false"), .select(2), .width(4)) multiplexer_21 (
    .in0(4'b0011), .in1(4'b0110), .in2(4'b1100), .out(shEnable), .sel(bytePos));  // open: in3

  assign BrUn = inst[13];
  assign BSel = inst[5];
  assign rd = inst[11:7];
  assign rs1 = inst[19:15];
  assign rs2 = inst[24:20];

  // Other names for the same wires on the sheet: byte1[7:0] = Reg2Data[7:0]; halfWord[15:0] = Reg2Data[15:0];
  //   aluFun7[1:0] = {inst[30], inst[25]}; aluFunc37[4:0] = {inst[14:12], inst[30], inst[25]};
  //   func7imm[6:0] = inst[31:25]; IaluFunc37[3:0] = {inst[14:12], inst[30]}; LorASel = inst[30];
  //   func3[2:0] = inst[14:12]; sign = inst[14]; opcode[6:0] = inst[6:0]; usefulOpcode[4:0] = inst[6:2]

  // Notes on the sheet:
  //   ALUSelDesjgn
  //   RegEN Design
  //   PCSel
  //   INPUTS to your circuit
  //   DON'T CHANGE THE LOCATIONS OF THE INPUTS AND OUTPUTS!
  //   OUTPUT from your circuit
  //   B_PCSel
  //   lh lb lw
  //   sh sb sw
endmodule
