// Logisim project cpu.circ as structural Verilog: 1 circuit, main circuit cpu
module cpu (
  input  clk,
  input  [31:0] INSTRUCTION,
  input  [31:0] READ_DATA,
  output [31:0] WRITE_ADDRESS,
  output [31:0] PROGRAM_COUNTER,
  output [31:0] ra,
  output [31:0] sp,
  output [31:0] t0,
  output [31:0] t1,
  output [31:0] t2,
  output [31:0] s0,
  output [31:0] s1,
  output [31:0] a0,
  output [31:0] tohost,
  output [3:0] WRITE_ENABLE,
  output [31:0] WRITE_DATA
);

  wire BrEq, BrLt, BrUn, BSel, CSRWen, MemRW, PCSel, RegWEn;
  wire [1:0] WBSel;
  wire [2:0] ImmSel;
  wire [3:0] ALUSel;
  wire [4:0] rd, rs1, rs2;
  wire [31:0] adder_1_out, adder_4_out, adder_5_out, adder_6_out, alu_UResult, aluResult, B, CSR_din, exePC,
       immediate, INSTRUCTION1, loadREAD_DATA, multiplexer_1_out, multiplexer_2_out, newPC, plusPC,
       Read_Data_1, Read_Data_2, UResult, Write_Data_t;

  Multiplexer #(.enable("false"), .width(32)) multiplexer_1 (
    .in0(adder_1_out), .in1(newPC), .out(multiplexer_1_out), .sel(PCSel));
  Adder #(.width(32)) adder_1 (.a(PROGRAM_COUNTER), .b(32'h4), .out(adder_1_out));  // open: cin, cout
  Register #(.width(32)) PC (.D(multiplexer_1_out), .clk(clk), .Q(PROGRAM_COUNTER));  // open: en, clr
  Register #(.width(32)) register_1 (.D(PROGRAM_COUNTER), .clk(clk), .Q(exePC));  // open: en, clr
  Multiplexer #(.enable("false"), .width(32)) multiplexer_2 (
    .in0(INSTRUCTION), .in1(32'h13), .out(multiplexer_2_out), .sel(PCSel));
  Register #(.width(32)) register_2 (.D(multiplexer_2_out), .clk(clk), .Q(INSTRUCTION1));  // open: en, clr
  Multiplexer #(.enable("false"), .width(32)) multiplexer_3 (.in0(immediate), .in1(Read_Data_2), .out(B), .sel(BSel));
  Adder #(.width(32)) adder_2 (.a(Read_Data_1), .b(immediate), .out(WRITE_ADDRESS));  // open: cin, cout
  Adder #(.width(32)) adder_3 (.a(exePC), .b(immediate), .out(plusPC));  // open: cin, cout
  control_logic control_logic_1 (
    .CSRWen(CSRWen), .rs1(rs1), .rs2(rs2), .rd(rd), .WRITE_ENABLE(WRITE_ENABLE),
    .load_read_data(loadREAD_DATA), .SwriteData(WRITE_DATA), .PCSel(PCSel), .RegWEn(RegWEn), .ImmSel(ImmSel),
    .BrUn(BrUn), .BSel(BSel), .ALUSel(ALUSel), .MemRW(MemRW), .WBSel(WBSel), .inst(INSTRUCTION1),
    .MEM_READ_DATA(READ_DATA), .bytePos(WRITE_ADDRESS[1:0]), .Reg2Data(Read_Data_2), .BrEq(BrEq),
    .Reg1Data(Read_Data_1), .BrLt(BrLt));  // open: ASel, CSRSel
  imm_gen imm_gen_1 (.inst(INSTRUCTION1), .ImmSel(ImmSel), .imm(immediate));
  Adder #(.width(32)) adder_4 (.a(Read_Data_1), .b(immediate), .out(adder_4_out));  // open: cin, cout
  regfile regfile_1 (
    .rs1(rs1), .rs2(rs2), .rd(rd), .Write_Data(Write_Data_t), .RegWEn(RegWEn), .clk(clk), .ra(ra), .sp(sp),
    .t0(t0), .t1(t1), .t2(t2), .s0(s0), .s1(s1), .a0(a0), .Read_Data_1(Read_Data_1), .Read_Data_2(Read_Data_2));
  branch_comp branch_comp_1 (.rs1(Read_Data_1), .rs2(Read_Data_2), .BrUn(BrUn), .BrEq(BrEq), .BrLt(BrLt));
  Multiplexer #(.enable("false"), .select(2), .width(32)) multiplexer_4 (
    .in0(plusPC), .in1(adder_4_out), .in3(plusPC), .out(newPC), .sel(INSTRUCTION1[3:2]));  // open: in2
  alu alu_1 (.Result(aluResult), .A(Read_Data_1), .B(B), .ALUSel(ALUSel));
  csr csr_1 (.CSR_address(12'h51e), .CSR_din(CSR_din), .CSR_WE(CSRWen), .clk(clk), .tohost(tohost));
  Multiplexer #(.enable("false"), .width(32)) multiplexer_5 (
    .in0(Read_Data_1), .in1(immediate), .out(CSR_din), .sel(INSTRUCTION1[14]));
  Adder #(.width(32)) adder_5 (.a(exePC), .b(32'h4), .out(adder_5_out));  // open: cin, cout
  Adder #(.width(32)) adder_6 (.a(exePC), .b(immediate), .out(adder_6_out));  // open: cin, cout
  Multiplexer #(.enable("false"), .select(2), .width(32)) multiplexer_6 (
    .in0(alu_UResult), .in1(loadREAD_DATA), .in2(adder_5_out), .out(Write_Data_t), .sel(WBSel));  // open: in3
  Multiplexer #(.enable("false"), .width(32)) multiplexer_7 (
    .in0(aluResult), .in1(UResult), .out(alu_UResult), .sel(INSTRUCTION1[2]));
  Multiplexer #(.enable("false"), .width(32)) multiplexer_8 (
    .in0(adder_6_out), .in1(immediate), .out(UResult), .sel(INSTRUCTION1[5]));

  // Other names for the same wires on the sheet: bytePos[1:0] = WRITE_ADDRESS[1:0]

  // Notes on the sheet:
  //   Output to IMEM
  //   IMEM (do **NOT** move this)
  //   Inputs from IMEM
  //   It is OK to move the PC, RegFile, ALU, MEM, Branch Comp, Imm Gen, and Control Logic to wherever is most convenient for you when constructing your CPU, and to delete this text
  //   Inputs/Outputs for testing. Do **NOT** move these.
  //   Outputs To DMEM
  //   DMEM (do **NOT** move this)
  //   Inputs From DMEM
endmodule
